// Logisim project water_tank.circ as structural Verilog
module thermal_io (
  input  S3,
  input  S2,
  input  S1,
  input  S0,
  output Q1_Level,
  output Q0_Level,
  output L1,
  output ALARM,
  output FULL,
  output L0,
  output Pump
);

  wire and_1_out, clock_1_out, digitallogiccircuit_1_a, digitallogiccircuit_1_b, digitallogiccircuit_1_c,
       digitallogiccircuit_1_d, digitallogiccircuit_1_e, digitallogiccircuit_1_f, digitallogiccircuit_1_g,
       not_1_out, not_2_out;
  wire [1:0] counter_1_q;

  not not_1 (not_1_out, S2);
  and and_1 (and_1_out, not_1_out, S1);
  D_Flip_Flop d_ff_1 (.D(S2), .clk(clock_1_out), .Q(Q1_Level));  // open: Qn, preset, reset
  Clock clock_1 (.out(clock_1_out));
  or or_1 (L0, and_1_out, S3);
  D_Flip_Flop d_ff_2 (.D(L0), .clk(clock_1_out), .Q(Q0_Level));  // open: Qn, preset, reset
  and and_2 (FULL, S2, L0);
  not not_2 (not_2_out, FULL);
  not not_3 (Pump, FULL);
  DigitalLogicCircuit digitallogiccircuit_1 (
    .Q1(Q1_Level), .Q2(Q0_Level), .a(digitallogiccircuit_1_a), .b(digitallogiccircuit_1_b),
    .c(digitallogiccircuit_1_c), .d(digitallogiccircuit_1_d), .e(digitallogiccircuit_1_e),
    .f(digitallogiccircuit_1_f), .g(digitallogiccircuit_1_g));
  Counter #(.max('h3), .width(2)) counter_1 (
    .clr(not_2_out), .load(FULL), .clk(clock_1_out), .Q(counter_1_q));  // open: up, count, D, carry
  _7_Segment_Display u_7_segment_display_1 (
    .g(digitallogiccircuit_1_g), .f(digitallogiccircuit_1_f), .a(digitallogiccircuit_1_a),
    .b(digitallogiccircuit_1_b), .e(digitallogiccircuit_1_e), .d(digitallogiccircuit_1_d),
    .c(digitallogiccircuit_1_c));  // open: dp
  and and_3 (ALARM, counter_1_q[0], counter_1_q[1]);

  assign L1 = S2;
endmodule

module DigitalLogicCircuit (
  input  Q1,
  input  Q2,
  output a,
  output b,
  output c,
  output d,
  output e,
  output f,
  output g
);

  wire not_1_out;

  not not_1 (not_1_out, Q1);
  not not_2 (e, Q2);
  or or_1 (a, e, Q1);
  or or_2 (c, not_1_out, Q2);
  or or_3 (d, e, Q1);
  and and_1 (f, not_1_out, e);

  assign b = 1'b1;
  assign g = Q1;
endmodule
